# Fritzing sketch DigitalThermometer (saved by Fritzing 0.9.3b)
breadboards: 1

parts:
  LCD1 = LCD screen
  DHT1 = DHT11 Humitidy and Temperature Sensor
  Arduino1 = Arduino Uno (Rev3)

nets:
  GND: LCD1.VSS, LCD1.R/W, LCD1.LED-, DHT1.GND, Arduino1.GND
  VDD: LCD1.VDD, DHT1.VDD, Arduino1.5V
  N1: LCD1.RS, Arduino1.D12/MISO
  N2: LCD1.E, Arduino1.D11_PWM/MOSI
  N3: LCD1.DB4, Arduino1.D5_PWM
  N4: LCD1.DB5, Arduino1.D4
  N5: LCD1.DB6, Arduino1.D3_PWM
  N6: LCD1.DB7, Arduino1.D2
  N7: DHT1.DATA, Arduino1.D8

custom parts:
  DHT11 Humitidy and Temperature Sensor: DHT11 Humidity and Temperature Sensor
